// Logisim project HCount.circ as structural Verilog: 3 circuits, main circuit VDP
module VDP (
);

  wire and_1_out, and_2_out, and_3_out, and_4_out, and_5_out, and_6_out, and_7_out, and_8_out, and_9_out,
       and_10_out, and_11_out, and_12_out, and_13_out, and_14_out, and_15_out, and_16_out, clock_1_out,
       d_ff_1_q, d_ff_2_q, d_ff_3_q, d_ff_4_q, j_k_ff_4_q, j_k_ff_5_q, j_k_ff_5_qn, j_k_ff_6_q,
       n74138_1_pin12, n74138_1_pin15, n74153_1_pin5, n74153_1_pin6, n74153_1_pin10, n74153_1_pin11,
       n74153_2_pin6, n74153_2_pin10, n74157_1_pin1, n74157_1_pin15, n74157_2_pin15, n74157_3_pin15,
       n74157_4_pin15, n74161_1_pin1, n74161_1_pin3, n74161_1_pin14, n74161_2_pin1, n74161_2_pin3,
       n74161_2_pin4, n74161_2_pin5, n74161_2_pin6, n74161_2_pin7, n74161_2_pin9, n74161_3_pin1,
       n74161_3_pin3, n74161_3_pin4, n74161_3_pin5, n74161_3_pin6, n74161_3_pin7, n74161_4_pin1,
       n74161_4_pin2, n74161_4_pin3, n74161_4_pin4, n74161_4_pin5, n74161_4_pin6, n74161_4_pin7,
       n74161_4_pin9, n74161_4_pin15, n74161_5_pin1, n74161_5_pin3, n74161_5_pin4, n74161_5_pin5,
       n74161_5_pin6, n74161_5_pin7, n74166_1_pin1, n74166_1_pin2, n74166_1_pin3, n74166_1_pin4,
       n74166_1_pin5, n74166_1_pin6, n74166_1_pin7, n74166_1_pin9, n74166_1_pin10, n74166_1_pin11,
       n74166_1_pin12, n74166_1_pin13, n74166_1_pin14, n74166_1_pin15, n74175_1_pin1, n74175_1_pin3,
       n74175_1_pin4, n74175_1_pin5, n74175_1_pin6, n74175_1_pin9, n74175_1_pin12, n74175_1_pin13,
       n74175_2_pin4, n74175_2_pin5, n74175_2_pin9, n74175_2_pin12, n74175_2_pin13, n74273_1_pin1,
       n74273_1_pin2, n74273_1_pin5, n74273_1_pin6, n74273_1_pin9, n74273_1_pin11, n74273_1_pin12,
       n74273_1_pin15, n74273_1_pin16, n74273_1_pin19, n74273_2_pin1, not_4_out, not_5_out, not_6_out,
       not_7_out, not_8_out, not_9_out, not_10_out, not_12_out, not_13_out, not_14_out, not_15_out,
       not_16_out, not_18_out, not_19_out, not_20_out, not_21_out, or_1_out, t_ff_1_q, t_ff_2_q, t_ff_3_q,
       t_ff_4_q;
  wire [2:2] n74161_1_pin11;
  wire [3:0] n74153_2_pin7;
  wire [7:0] multiplexer_1_out, multiplexer_3_out, n74157_1_pin3, n74273_1_pin3, register_1_q,
       rgb_video_1_p6, rom_1_data, rom_2_data;
  wire [8:0] j_k_ff_2_q, n74161_1_pin13;

  // NOT_Gate not_1 is placed but not wired
  J_K_Flip_Flop j_k_ff_1 ();  // open: J, clk, K, Q, Qn, preset, reset
  Clock clock_1 (.out(clock_1_out));
  T_Flip_Flop t_ff_1 (.clk(n74161_1_pin11[2]), .T(1'b1), .Q(t_ff_1_q));  // open: Qn, preset, reset
  T_Flip_Flop t_ff_2 (.clk(t_ff_1_q), .T(1'b1), .Q(t_ff_2_q));  // open: Qn, preset, reset
  T_Flip_Flop t_ff_3 (.clk(t_ff_2_q), .T(1'b1), .Q(t_ff_3_q));  // open: Qn, preset, reset
  T_Flip_Flop t_ff_4 (.clk(t_ff_3_q), .T(1'b1), .Q(t_ff_4_q));  // open: Qn, preset, reset
  _74161 #(.ShowInternalStructure("true")) u_74161_1 (
    .pin1(n74161_1_pin1), .pin2(clock_1_out), .pin3(n74161_1_pin3), .pin4(n74161_1_pin3),
    .pin5(n74161_1_pin3), .pin6(n74161_1_pin3), .pin7(n74161_1_pin3), .pin14(n74161_1_pin14),
    .pin13(n74161_1_pin13[0]), .pin12(n74161_1_pin13[1]), .pin11(n74161_1_pin11[2]), .pin10(n74161_1_pin3),
    .pin9(n74161_1_pin3));  // open: pin15
  _74161 #(.ShowInternalStructure("true")) u_74161_2 (
    .pin1(n74161_2_pin1), .pin2(n74161_1_pin11[2]), .pin3(n74161_2_pin3), .pin4(n74161_2_pin4),
    .pin5(n74161_2_pin5), .pin6(n74161_2_pin6), .pin7(n74161_2_pin7), .pin14(n74161_1_pin13[7]),
    .pin13(n74161_1_pin13[8]), .pin10(n74161_2_pin7), .pin9(n74161_2_pin9));  // open: pin15, pin12, pin11
  _74161 #(.ShowInternalStructure("true")) u_74161_3 (
    .pin1(n74161_3_pin1), .pin2(n74161_1_pin11[2]), .pin3(n74161_3_pin3), .pin4(n74161_3_pin4),
    .pin5(n74161_3_pin5), .pin6(n74161_3_pin6), .pin7(n74161_3_pin7), .pin15(n74161_2_pin7),
    .pin14(n74161_1_pin13[3]), .pin13(n74161_1_pin13[4]), .pin12(n74161_1_pin13[5]),
    .pin11(n74161_1_pin13[6]), .pin10(n74161_3_pin7), .pin9(n74161_2_pin9));
  _74161 #(.ShowInternalStructure("true")) u_74161_4 (
    .pin1(n74161_4_pin1), .pin2(n74161_4_pin2), .pin3(n74161_4_pin3), .pin4(n74161_4_pin4),
    .pin5(n74161_4_pin5), .pin6(n74161_4_pin6), .pin7(n74161_4_pin7), .pin15(n74161_4_pin15),
    .pin14(j_k_ff_2_q[4]), .pin13(j_k_ff_2_q[5]), .pin12(j_k_ff_2_q[6]), .pin11(j_k_ff_2_q[7]),
    .pin10(n74161_4_pin7), .pin9(n74161_4_pin9));
  _74161 #(.ShowInternalStructure("true")) u_74161_5 (
    .pin1(n74161_5_pin1), .pin2(n74161_4_pin2), .pin3(n74161_5_pin3), .pin4(n74161_5_pin4),
    .pin5(n74161_5_pin5), .pin6(n74161_5_pin6), .pin7(n74161_5_pin7), .pin15(n74161_4_pin7),
    .pin14(j_k_ff_2_q[0]), .pin13(j_k_ff_2_q[1]), .pin12(j_k_ff_2_q[2]), .pin11(j_k_ff_2_q[3]),
    .pin10(n74161_5_pin7), .pin9(n74161_4_pin9));
  J_K_Flip_Flop j_k_ff_2 (
    .J(n74161_4_pin15), .clk(n74161_4_pin2), .K(and_3_out), .Q(j_k_ff_2_q[8]));  // open: Qn, preset, reset
  and and_1 (and_1_out, n74161_1_pin11[2], n74161_1_pin13[1], n74161_1_pin13[0], n74161_1_pin14);
  and and_2 (and_2_out, n74161_1_pin13[7], n74161_1_pin13[8], n74161_1_pin13[6]);
  not not_2 (n74161_2_pin9, and_2_out);
  and and_3 (and_3_out, j_k_ff_2_q[8], and_4_out);
  not not_3 (n74161_4_pin9, and_3_out);
  not not_4 (not_4_out, n74161_1_pin13[7]);
  not not_5 (not_5_out, j_k_ff_2_q[7]);
  and and_4 (and_4_out, j_k_ff_2_q[2], j_k_ff_2_q[0]);
  and and_5 (and_5_out, n74161_1_pin13[8], not_4_out, n74161_1_pin13[6]);
  and and_6 (and_6_out, n74161_1_pin13[3], n74161_1_pin13[7], n74161_1_pin13[8]);
  D_Flip_Flop d_ff_1 (.clk(n74161_4_pin2), .D(and_3_out), .Q(d_ff_1_q));  // open: Qn, preset, reset
  and and_7 (and_7_out, and_5_out, n74161_2_pin7, j_k_ff_5_qn);
  and and_8 (and_8_out, and_5_out, n74161_1_pin13[5], n74161_1_pin13[4]);
  _74138 #(.ShowInternalStructure("true")) u_74138_1 (
    .pin1(j_k_ff_2_q[3]), .pin2(j_k_ff_2_q[4]), .pin3(j_k_ff_2_q[5]), .pin4(j_k_ff_2_q[8]), .pin5(not_5_out),
    .pin6(j_k_ff_2_q[6]), .pin15(n74138_1_pin15), .pin12(n74138_1_pin12));  // open: pin7, pin14, pin13, pin11, pin10, pin9
  and and_9 (and_9_out, and_5_out, not_6_out, n74161_1_pin13[4]);
  not not_6 (not_6_out, and_8_out);
  not not_7 (not_7_out, n74161_1_pin13[8]);
  not not_8 (not_8_out, n74138_1_pin12);
  not not_9 (not_9_out, n74138_1_pin15);
  and and_10 (and_10_out, not_8_out, and_4_out);
  not not_10 (not_10_out, n74161_1_pin11[2]);
  J_K_Flip_Flop #(.trigger("falling")) j_k_ff_3 (
    .J(and_9_out), .clk(not_10_out), .K(and_8_out), .Q(n74161_4_pin2));  // open: Qn, preset, reset
  D_Flip_Flop d_ff_2 (.clk(n74161_1_pin11[2]), .D(not_7_out), .Q(d_ff_2_q));  // open: Qn, preset, reset
  J_K_Flip_Flop #(.trigger("falling")) j_k_ff_4 (
    .J(and_7_out), .clk(not_10_out), .K(and_6_out), .Q(j_k_ff_4_q));  // open: Qn, preset, reset
  J_K_Flip_Flop #(.trigger("falling")) j_k_ff_5 (
    .J(and_10_out), .clk(not_10_out), .K(j_k_ff_2_q[5]), .Q(j_k_ff_5_q), .Qn(j_k_ff_5_qn));  // open: preset, reset
  J_K_Flip_Flop #(.trigger("falling")) j_k_ff_6 (
    .J(d_ff_1_q), .clk(not_10_out), .K(not_9_out), .Q(j_k_ff_6_q));  // open: Qn, preset, reset
  and and_11 (and_11_out, d_ff_2_q, j_k_ff_6_q);
  not not_11 (n74161_1_pin13[2], n74161_1_pin11[2]);
  // Probe on {n74161_1_pin13[8:3], n74161_1_pin11[2], n74161_1_pin13[1:0]}
  or or_1 (or_1_out, and_12_out, and_13_out);
  // RGB_Video #(.cursor("No Cursor"), .height(262), .scale(1), .width(458)) rgb_video_1: pin names not known; wires that end beside it: 1'b0, n74161_1_pin14, 1'b1, n74161_1_pin13, j_k_ff_2_q, rgb_video_1_p6
  // Probe on j_k_ff_2_q
  and and_12 (and_12_out, n74161_1_pin13[0], 1'b0);
  and and_13 (and_13_out, n74161_1_pin14, not_12_out);
  Multiplexer #(.width(8)) multiplexer_1 (.in0(register_1_q), .in1(8'hb), .out(multiplexer_1_out), .sel(j_k_ff_4_q));
  not not_12 (not_12_out, 1'b0);
  Multiplexer #(.width(8)) multiplexer_2 (.in0(multiplexer_3_out), .in1(8'hc), .out(rgb_video_1_p6), .sel(j_k_ff_5_q));
  Multiplexer #(.width(8)) multiplexer_3 (
    .in0(multiplexer_1_out), .in1(8'hd), .out(multiplexer_3_out), .sel(n74161_4_pin2));
  Register register_1 (.D({4'b0000, n74153_2_pin7}), .en(1'b1), .Q(register_1_q), .clk(or_1_out));  // open: clr
  // Probe on j_k_ff_5_q
  // OR_Gate or_2 is placed but not wired
  _74273 #(.ShowInternalStructure("true")) u_74273_1 (
    .pin1(n74273_1_pin1), .pin2(n74273_1_pin2), .pin3(n74273_1_pin3[0]), .pin4(n74273_1_pin3[1]),
    .pin5(n74273_1_pin5), .pin6(n74273_1_pin6), .pin7(n74273_1_pin3[2]), .pin8(n74273_1_pin3[3]),
    .pin9(n74273_1_pin9), .pin19(n74273_1_pin19), .pin18(n74273_1_pin3[7]), .pin17(n74273_1_pin3[6]),
    .pin16(n74273_1_pin16), .pin15(n74273_1_pin15), .pin14(n74273_1_pin3[5]), .pin13(n74273_1_pin3[4]),
    .pin12(n74273_1_pin12), .pin11(n74273_1_pin11));
  not not_13 (not_13_out, and_1_out);
  not not_14 (not_14_out, not_13_out);
  not not_15 (not_15_out, and_11_out);
  D_Flip_Flop d_ff_3 (.clk(n74166_1_pin7), .D(n74166_1_pin13), .Q(d_ff_3_q), .reset(not_16_out));  // open: Qn, preset
  not not_16 (not_16_out, 1'b0);
  _74166 #(.ShowInternalStructure("true")) u_74166_1 (
    .pin1(n74166_1_pin1), .pin2(n74166_1_pin2), .pin3(n74166_1_pin3), .pin4(n74166_1_pin4),
    .pin5(n74166_1_pin5), .pin6(n74166_1_pin6), .pin7(n74166_1_pin7), .pin15(n74166_1_pin15),
    .pin14(n74166_1_pin14), .pin13(n74166_1_pin13), .pin12(n74166_1_pin12), .pin11(n74166_1_pin11),
    .pin10(n74166_1_pin10), .pin9(n74166_1_pin9));
  or or_3 (n74166_1_pin15, not_18_out, and_16_out);
  _74153 #(.ShowInternalStructure("true")) u_74153_1 (
    .pin1(not_15_out), .pin2(d_ff_3_q), .pin3(n74273_1_pin16), .pin4(n74273_1_pin6), .pin5(n74153_1_pin5),
    .pin6(n74153_1_pin6), .pin7(n74153_2_pin7[2]), .pin15(not_15_out), .pin14(n74166_1_pin13),
    .pin13(n74273_1_pin19), .pin12(n74273_1_pin9), .pin11(n74153_1_pin11), .pin10(n74153_1_pin10),
    .pin9(n74153_2_pin7[3]));
  not not_17 (n74166_1_pin7, n74161_1_pin14);
  not not_18 (not_18_out, not_14_out);
  _74175 #(.ShowInternalStructure("true")) u_74175_1 (
    .pin1(n74175_1_pin1), .pin3(n74175_1_pin3), .pin4(n74175_1_pin4), .pin5(n74175_1_pin5),
    .pin6(n74175_1_pin6), .pin14(n74153_1_pin11), .pin13(n74175_1_pin13), .pin12(n74175_1_pin12),
    .pin11(n74153_1_pin5), .pin9(n74175_1_pin9));  // open: pin2, pin7, pin15, pin10
  _74157 #(.ShowInternalStructure("true")) u_74157_1 (
    .pin1(n74157_1_pin1), .pin2(n74273_1_pin3[0]), .pin3(n74157_1_pin3[0]), .pin4(n74175_1_pin4),
    .pin5(n74273_1_pin3[1]), .pin6(n74157_1_pin3[1]), .pin7(n74175_1_pin5), .pin15(n74157_1_pin15),
    .pin14(n74273_1_pin3[3]), .pin13(n74157_1_pin3[3]), .pin12(n74175_1_pin13), .pin11(n74273_1_pin3[2]),
    .pin10(n74157_1_pin3[2]), .pin9(n74175_1_pin12));
  D_Flip_Flop d_ff_4 (.clk(n74166_1_pin7), .D(not_14_out), .Q(d_ff_4_q));  // open: Qn, preset, reset
  _74153 #(.ShowInternalStructure("true")) u_74153_2 (
    .pin1(not_15_out), .pin2(d_ff_3_q), .pin3(n74273_1_pin12), .pin4(n74273_1_pin2), .pin5(n74175_1_pin3),
    .pin6(n74153_2_pin6), .pin7(n74153_2_pin7[0]), .pin15(not_15_out), .pin14(n74166_1_pin13),
    .pin13(n74273_1_pin15), .pin12(n74273_1_pin5), .pin11(n74175_1_pin6), .pin10(n74153_2_pin10),
    .pin9(n74153_2_pin7[1]));
  _74175 #(.ShowInternalStructure("true")) u_74175_2 (
    .pin1(n74175_1_pin1), .pin2(n74153_2_pin6), .pin4(n74175_2_pin4), .pin5(n74175_2_pin5),
    .pin7(n74153_2_pin10), .pin15(n74153_1_pin10), .pin13(n74175_2_pin13), .pin12(n74175_2_pin12),
    .pin10(n74153_1_pin6), .pin9(n74175_2_pin9));  // open: pin3, pin6, pin14, pin11
  _74157 #(.ShowInternalStructure("true")) u_74157_2 (
    .pin1(n74157_1_pin1), .pin2(n74273_1_pin3[4]), .pin3(n74157_1_pin3[0]), .pin4(n74175_2_pin4),
    .pin5(n74273_1_pin3[5]), .pin6(n74157_1_pin3[1]), .pin7(n74175_2_pin5), .pin15(n74157_2_pin15),
    .pin14(n74273_1_pin3[7]), .pin13(n74157_1_pin3[3]), .pin12(n74175_2_pin13), .pin11(n74273_1_pin3[6]),
    .pin10(n74157_1_pin3[2]), .pin9(n74175_2_pin12));
  not not_19 (not_19_out, n74157_1_pin1);
  or or_4 (n74175_1_pin1, not_7_out, not_19_out);
  and and_14 (and_14_out, and_16_out, n74157_1_pin3[4]);
  or or_5 (n74175_1_pin9, and_14_out, 1'b0);
  and and_15 (and_15_out, and_16_out, not_20_out);
  or or_6 (n74175_2_pin9, and_15_out, 1'b0);
  not not_20 (not_20_out, n74157_1_pin3[4]);
  and and_16 (and_16_out, n74157_1_pin1, d_ff_4_q, not_21_out, n74157_1_pin3[6], n74157_1_pin3[7]);
  not not_21 (not_21_out, n74157_1_pin3[5]);
  // Probe on j_k_ff_2_q
  ROM #(.addrWidth(11)) rom_1 (.addr({n74157_1_pin3, j_k_ff_2_q[2:0]}), .data(rom_1_data));
  _74157 #(.ShowInternalStructure("true")) u_74157_3 (
    .pin1(n74157_1_pin1), .pin2(n74157_1_pin3[4]), .pin3(rom_1_data[4]), .pin4(n74166_1_pin10),
    .pin5(n74157_1_pin3[5]), .pin6(rom_1_data[5]), .pin7(n74166_1_pin11), .pin15(n74157_3_pin15),
    .pin14(n74157_1_pin3[7]), .pin13(rom_1_data[7]), .pin12(n74166_1_pin14), .pin11(n74157_1_pin3[6]),
    .pin10(rom_1_data[6]), .pin9(n74166_1_pin12));
  _74157 #(.ShowInternalStructure("true")) u_74157_4 (
    .pin1(n74157_1_pin1), .pin2(n74157_1_pin3[0]), .pin3(rom_1_data[0]), .pin4(n74166_1_pin2),
    .pin5(n74157_1_pin3[1]), .pin6(rom_1_data[1]), .pin7(n74166_1_pin3), .pin15(n74157_4_pin15),
    .pin14(n74157_1_pin3[3]), .pin13(rom_1_data[3]), .pin12(n74166_1_pin5), .pin11(n74157_1_pin3[2]),
    .pin10(rom_1_data[2]), .pin9(n74166_1_pin4));
  ROM #(.addrWidth(12)) rom_2 (.addr({2'b00, j_k_ff_2_q[7:3], n74161_1_pin13[7:3]}), .data(rom_2_data));
  // Probe on {2'b00, j_k_ff_2_q[7:3], n74161_1_pin13[7:3]}
  _74273 #(.ShowInternalStructure("true")) u_74273_2 (
    .pin1(n74273_2_pin1), .pin2(n74157_1_pin3[0]), .pin3(rom_2_data[0]), .pin4(rom_2_data[1]),
    .pin5(n74157_1_pin3[1]), .pin6(n74157_1_pin3[2]), .pin7(rom_2_data[2]), .pin8(rom_2_data[3]),
    .pin9(n74157_1_pin3[3]), .pin19(n74157_1_pin3[7]), .pin18(rom_2_data[7]), .pin17(rom_2_data[6]),
    .pin16(n74157_1_pin3[6]), .pin15(n74157_1_pin3[5]), .pin14(rom_2_data[5]), .pin13(rom_2_data[4]),
    .pin12(n74157_1_pin3[4]), .pin11(not_10_out));
  // also tied to GND on the sheet: {n74161_2_pin3, n74161_2_pin4, n74161_2_pin5, n74161_2_pin6, n74161_3_pin3, n74161_3_pin4, n74161_3_pin5, n74161_3_pin6, n74161_4_pin3, n74161_4_pin4, n74161_4_pin5, n74161_4_pin6, n74161_5_pin3, n74161_5_pin4, n74161_5_pin5, n74161_5_pin6, n74166_1_pin1, n74166_1_pin6, n74273_1_pin11, n74157_1_pin15, n74157_2_pin15, n74273_1_pin3[2], n74273_1_pin3[3], n74273_1_pin3[4], n74157_3_pin15, n74157_4_pin15}
  // also tied to VCC on the sheet: {n74161_1_pin1, n74161_2_pin1, n74161_3_pin1, n74161_3_pin7, n74161_4_pin1, n74161_5_pin1, n74161_5_pin7, n74161_1_pin3, n74273_1_pin1, n74166_1_pin9, n74273_1_pin3[0], n74273_1_pin3[1], n74273_1_pin3[5], n74273_1_pin3[6], n74273_1_pin3[7], n74157_1_pin1, n74273_2_pin1}

  // Notes on the sheet:
  //   U30-U44 (~U39)
  //   5 Counter + 9 Decode
  //   U35 4-bit Counter
  //   U36 4-bit Counter
  //   U40 4-bit Counter
  //   U41 4-bit Counter
  //   U43 Dual JK (1/2)
  //   U30 Dual DFF
  //   U31 Dual JK
  //   U32 Tripe 3-AND
  //   U33 Dual JK
  //   U34 Quad 2-AND
  //   U37 Tripe 3-AND
  //   U38 Hex Inverter
  //   U42 1 of 8 Decoder
  //   U44 Hex Inverter
  //   U44C
  //   U43B
  //   CLK
  //   14.31818 MHz
  //   HSync
  //   MUST update Address on /CLK mid-cycle
  //   Address setup for mid-high-CLK RAS
  //   13 Chips H & V
  //   6-bit H-Count
  //   [0-56]
  //   U35
  //   U36
  //   9-bit V-Count
  //   U43A
  //   U40
  //   U41
  //   VScan= ~(d8+(d7•d6))
  //   U38A
  //   Border
  //   VBlank = 76~543 + 765~4~3 + 765~4~2
  //   VSync = VBL • ~(d4 + d3 + d2) • (d1 + d0)
  //   N/A
  //   7.15909 MHz
  //   3.579545 MHz
  //   1.7897725 MHz
  //   0.894886 MHz
  //   RHC 56
  //   111xxx
  //   U32A
  //   RVC 261
  //   (100 000 101)
  //   RVC
  //   U34B
  //   U38F
  //   1x1
  //   U34A
  //   Work-around for incorrectly timed RCO output
  //   1 in 16
  //   SHB 40
  //   101xxx
  //   U32B
  //   U38B
  //   U44A
  //   U30B
  //   RCB 49
  //   11xxx1
  //   U32C
  //   011
  //   1 Line Delay (261->0)
  //   Not VSync
  //   SCB 47
  //   101111
  //   U37C
  //   VSync
  //   Not HBlank
  //   U38C
  //   RHS 46
  //   10111x
  //   U37B
  //   U42
  //   HBlank
  //   SHS 42
  //   101x1x
  //   U37A
  //   U38D
  //   011000xxx
  //   011011xxx
  //   011100xxx
  //   Colorburst
  //   Not Burst
  //   VBlank
  //   Not VBlank
  //   Fetch
  //   U44B
  //   U44D
  //   HSync
  //   Not HSync
  //   Scan
  //   NotScan
  //   Negate Negative Edge (74LS73)
  //   Must be rising-edge for 8px delay
  //   011011101
  //   U34C
  //   xxx100000
  //   000000000 (0)
  //   011000000 (192)
  //   U44E
  //   U31A
  //   HSync
  //   U30A
  //   H-Visible
  //   U31B
  //   Colorburst
  //   U33A
  //   VSync
  //   U33B
  //   V-Visible
  //   HBlank
  //   Not HBlank
  //   --
  //   --
  //   VBlank
  //   Not VBlank
  //   7.15909 MHz
  //   Visible
  //   U34D
  //   VSync
  //   Not VSync
  //   VSync
  //   Not VSync
  //   HSync
  //   Not HSync
  //   Scan
  //   NotScan
  //   HCount
  //   SimVGA
  //   VCount
  //   U57C
  //   U57D
  //   HSync
  //   Burst
  //   DAC Latch
  //   74LS175
  //   VSync
  //   VSync
  //   VDP_2BPP
  //   Most home computers/consoles
  //   use 0 IRE for both Black and Blanking level
  //   (that would eliminate HBlank and VBlank)
  //   U58C
  //   Fetch
  //   Visible
  //   Last PCLK in the CLK cycle
  //   2BPP
  //   Visible
  //   U52
  //   COL2/3
  //   \PCLK
  //   U38E
  //   Delay beyond \PCLK edge
  //   U45A
  //   Active Low
  //   Border
  //   Select Color 0
  //   LOAD on last \PCLK in CLK cycle
  //   U39
  //   Shift Register
  //   2BPP D1
  //   IOQ_FE
  //   nLoad
  //   U58D
  //   PCLK
  //   U44F
  //   \PCLK
  //   U46
  //   Col MUX 2,3
  //   U48
  //   U50
  //   FG MUX
  //   U45B
  //   Y3
  //   Y2
  //   Inhibit Attribute Load
  //   U47
  //   Col MUX 0,1
  //   U49
  //   U51
  //   BG MUX
  //   Hold FG/BG in Reset until Fetch begins
  //   Y1
  //   Y0
  //   nFetch
  //   Data Bus
  //   LoadQ on \PCLK
  //   nText
  //   U58D
  //   nCLR
  //   VDP_TEXT
  //   Inhibit Attribute Load
  //   Text
  //   U58A
  //   U58B
  //   IO Load
  //   Palette
  //   IOQ_FD
  //   Cx Load
  //   Dx Load
  //   LoadQ on \PCLK
  //   Attr Load
  //   U56C
  //   U57A
  //   Bus CLK 0.89 MHz
  //   Cx/Dx (110x)
  //   Cx/Dx AND Text
  //   V[0..2]
  //   MUST latch at /CLK mid-cycle for VDP
  //   H[3..8]
  //   Shift Reg
  //   V[3..8]
  //   Char
  //   line
  //   contents of rom_1 (hex, n*v repeats v):
  //   aa 55 aa 55 aa 55 aa 55 aa 41 aa 4 aa 10 aa 4 aa 0 aa 0 aa 0 aa 0 88 0 a2 0 24 0 8a 0 8 0 82 0 0 20
  //   2 4*0 1f 1f 18 18 18 0 0 0 f8 f8 6*18 1f 1f 0 0 0 18 18 18 f8 f8 6*0 ff ff 0 0 0 11*18 ff ff 6*0 ff
  //   ff 6*18 1f 1f 6*18 f8 f8 6*18 ff ff 18 18 18 1 3 6 c 18 30 60 c0 80 c0 60 30 18 c 6 3 c0 60 30 18 c
  //   6 3 1 3 6 c 18 30 60 c0 80 c3 66 2c 18 34 66 c3 81 0 0 18 3c 3c 18 4*0 18 24 24 18 0 0 10 38 7c fe
  //   7c 38 10 0 10 38 54 fe 54 10 38 0 44 ee fe fe 7c 38 10 0 10 38 7c fe 6c 10 38 0 0 2 0 0 10 1 5*0 8
  //   7*0 18 18 0 0 0 cc 66 33 99 cc 66 33 99 33 66 cc 99 33 66 cc 99 9*0 18 18 18 0 18 18 0 0 36 36 5*0
  //   36 36 7f 36 7f 36 36 0 8 3e 68 3e b 3e 8 0 21 52 24 8 12 25 42 0 30 48 68 30 5b 4c 36 0 18 18 30 5*0
  //   18 30 60 60 60 30 18 0 c 6 3 3 3 6 c 0 0 36 1c 7f 1c 36 0 0 0 c c 3f c c 6*0 18 18 30 5*0 3f 8*0 18
  //   18 0 0 3 6 c 18 30 60 0 0 3c 66 6e 76 66 3c 0 0 18 38 78 18 18 7e 0 0 3c 66 c 18 30 7e 0 0 3c 66 c 6
  //   66 3c 0 0 c 1c 2c 6c 7e c 0 0 7e 60 7c 6 66 3c 0 0 3c 60 7c 66 66 3c 0 0 7e 6 c 18 30 30 0 0 3c 66
  //   3c 66 66 3c 0 0 3c 66 66 3e 6 3c 0 0 0 c c 0 c c 0 0 0 c c 0 c 18 0 0 6 c 18 18 c 6 0 0 0 3e 0 3e
  //   4*0 30 18 c c 18 30 0 0 3c 66 c 18 0 18 0 1e 21 4d 55 4a 20 1e 0 0 3c 66 7e 66 66 66 0 0 7c 66 7c 66
  //   66 7c 0 0 3c 66 60 60 66 3c 0 0 78 6c 66 66 6c 78 0 0 7e 60 7c 60 60 7e 0 0 7e 60 7c 60 60 60 0 0 3c
  //   66 60 6e 66 3c 0 0 66 66 7e 66 66 66 0 0 7e 4*18 7e 0 0 3e c c c 6c 38 0 0 66 6c 78 78 6c 66 0 0
  //   5*60 7e 0 0 63 77 7f 6b 63 63 0 0 66 76 7e 6e 66 66 0 0 3c 4*66 3c 0 0 7c 66 66 7c 60 60 0 0 3c 66
  //   66 6a 6c 36 0 0 7c 66 66 7c 6c 66 0 0 3c 62 3c 6 66 3c 0 0 7e 5*18 0 0 5*66 3c 0 0 4*66 3c 18 0 0 63
  //   63 6b 7f 77 63 0 0 66 66 3c 3c 66 66 0 0 66 66 3c 18 18 18 0 0 7e c 18 30 60 7e 0 0 7c 4*60 7c 0 0
  //   60 30 18 c 6 3 0 0 3e 4*6 3e 0 0 18 3c 66 11*0 7f 0 60 30 18 6*0 3c 6 3e 66 3c 0 0 60 7c 66 66 66 7c
  //   0 0 0 3c 66 60 66 3c 0 0 6 3e 66 66 66 3e 0 0 0 3c 66 7c 60 3c 0 0 1e 30 7c 30 30 30 0 0 0 3c 66 66
  //   3e 6 3c 0 60 60 6c 76 66 66 0 0 18 0 38 18 18 3c 0 0 c 0 1c c c 6c 38 0 60 66 6c 78 6c 66 0 0 38
  //   4*18 3c 0 0 0 36 7f 6b 6b 63 0 0 0 7c 4*66 0 0 0 3c 66 66 66 3c 0 0 0 7c 66 66 7c 60 60 0 0 3e 66 66
  //   3e 6 6 0 0 6c 76 60 60 60 0 0 0 3c 60 3c 6 3c 0 0 30 7c 30 30 30 1c 0 0 0 4*66 3c 0 0 0 66 66 66 3c
  //   18 0 0 0 63 6b 6b 7f 36 0 0 0 66 3c 18 3c 66 0 0 0 66 66 66 3e 6 3c 0 0 7e c 18 30 7e 0 0 6 c c 18 c
  //   c 6 0 7*18 0 30 18 18 c 18 18 30 0 0 0 31 6b 46 5*0 18 24 42 42 7e 256*0 1 3 7 f 1f 3f 7f ff 80 c0
  //   e0 f0 f8 fc fe ff 4*0 1 3 7 f 4*0 80 c0 e0 f0 1 2 4 8 10 20 40 80 80 40 20 10 8 4 2 1 4*0 1 2 4 8
  //   4*0 80 40 20 10 0 3c 42 81 24 e7 3c 1 ff 7*80 ff 7*0 ff 7*1 ff 6*81 ff 18 24 42 81 81 42 24 18 18 18
  //   3c 3c 7e 7e ff ff 18 18 24 24 42 42 81 81 ff 7f 3f 1f f 7 3 1 ff fe fc f8 f0 e0 c0 80 f 7 3 1 4*0 f0
  //   e0 c0 80 4*0 80 40 20 10 8 4 2 1 1 2 4 8 10 20 40 80 8 4 2 1 4*0 10 20 40 80 4*0 e3 95 89 a2 bc a0
  //   a0 0 8*80 a5 0 81 0 0 81 0 a5 8*1 0 0 3c 24 24 3c 0 0 18 3c 7e ff ff 7e 3c 18 ff ff 7e 7e 3c 3c 18
  //   18 81 81 42 42 24 24 18 18 57*0 c a 9 4 2 1 0 0 30 50 90 20 40 80 0 7*80 ff 7*0 ff 7*1 ff 3 f 3f ff
  //   ff 3f f 3 c0 f0 fc ff ff fc f0 c0 3 c 30 c0 c0 30 c 3 c0 30 c 3 3 c 30 c0 20*0 f 8 8 8 4*0 ff 7*0 f0
  //   10 10 10 8*8 44 48 50 60 4*0 8*10 8 8 8 f 7*0 ff 4*0 10 10 10 f0 5*0 18 24 42 24 18 4*0 18 76 24 18
  //   5*0 2a 22 2 4*0 2 4c 30 7*0 42 3c 14*0 4*f 4*0 4*f0 4*0 4*ff 4*f 4*0 12*f 4*f0 4*f 4*ff 4*f0 4*0
  //   4*f0 4*f 12*f0 8*ff 4*0 4*ff 4*f 4*ff 4*f0 8*ff 8*0 8*3 8*c 8*f 8*30 8*33 8*3c 8*3f 8*c0 8*c3 8*cc
  //   8*cf 8*f0 8*f3 8*fc 8*ff
  //   CharROM
  //   Data ready by /CLK mid-cycle for VDP
  //   U54
  //   CharROM
  //   Bypass
  //   U55
  //   contents of rom_2 (hex, n*v repeats v):
  //   78 d8 a2 ff 9a a2 1 86 d9 ca 20 ec fe a0 23 20 9e fd a9 10 85 dc a9 5 85 75 85 77 a2 0 86 76 86 cc
  //   86 cd 86 cf 38 a5 dc e5 75 85 ce 20 e9 fa a0 3c 20 9e fd d8 20 ca ff a0 49 20 9e fd a2 ff 9a 20 85
  //   fe 84 c9 20 d2 fd a0 0 20 ef f0 c9 0 f0 ec 20 37 fa d0 2a a2 f3 a9 0 20 d7 f4 90 13 20 66 f0 4c 3e
  //   f0 29 7 a aa bd 35 f6 48 bd 34 f6 48 60 20 c2 f0 a9 1 85 7d a0 0 84 7c 4c 29 f7 a5 cf 85 78 a5 ce 85
  //   79 30 6 20 c2 f0 4c 3e f0 a0 e5 20 a4 fd a0 e9 20 9e fd 4c 3e f0 48 a0 c2 20 a4 fd 68 20 e5 fd 20 d2
  //   fd 4c 3e f0 a0 f7 20 9e fd a5 d2 30 fc 4c 3e f0 a0 ca 4c 93 f0 4c 4f f1 88 c8 20 ef f0 20 f9 f0 b0
  //   ee aa bd 0 f4 a2 f4 20 d7 f4 90 e8 9 c0 20 f2 f5 29 31 aa bd 1 f6 85 c8 29 f aa a9 f1 48 bd 21 f6 48
  //   60 b9 0 1 c8 c9 20 f0 f8 88 60 b9 0 1 29 df 38 e9 41 c9 1a 60 60 a5 c8 4*6a 29 7 85 c8 d0 3 20 e8 f1
  //   20 35 f2 c6 c8 d0 f6 60 20 5 f1 20 35 f2 90 6 20 35 f2 90 1 60 a9 0 4c f2 f5 20 e0 f1 20 f2 f5 85 c6
  //   b1 c4 c8 20 f2 f5 c6 c6 d0 f6 60 4c 5 f2 20 5 f2 20 e8 f1 20 35 f2 60 20 35 f2 85 c9 a9 3d 20 ea f1
  //   20 35 f2 c5 c9 d0 1 60 a0 e1 4c 93 f0 20 35 f2 a9 28 20 ea f1 20 35 f2 a9 29 20 ea f1 60 20 35 f2 29
  //   1 d0 e3 a9 3d 20 ea f1 20 35 f2 a2 f5 20 1d f2 90 41 20 35 f2 a2 f5 20 1d f2 90 93 4c 35 f2 20 ef f0
  //   20 f9 f0 b0 88 4c 35 f2 20 35 f2 a2 f5 20 1d f2 90 1f 90 5 20 34 f2 90 0 60 20 ee f5 86 c8 20 35 f2
  //   e6 c8 20 f8 f1 f0 f6 88 a5 c8 a2 0 95 c2 60 84 c9 a0 ca 20 a4 fd a4 c9 20 ad f6 20 d2 fd 4c 3e f0 86
  //   c6 a5 c9 18 e5 c6 60 a9 2c 85 ca 20 ef f0 c5 ca d0 2 c8 60 4c 9e f0 a9 2c 85 ca 20 ef f0 c5 ca d0 1
  //   c8 60 a9 23 20 ea f1 20 37 fa a5 ce d0 9 a5 cf c9 4 b0 3 4c f2 f5 4c 81 f9 20 ef f0 84 ca ca 88 e8
  //   c8 bd 0 f5 d1 c0 f0 f7 c9 80 b0 2 a4 ca 60 60 203*0 4c 49 53 54 c0 52 55 4e c1 41 52 54 c2 53 41 56
  //   45 c3 41 55 54 4f c4 44 45 4c c5 4e 45 57 c6 4f 4c 44 87 18 92 93 94 95 96 90 d d 50 69 78 69 65 20
  //   42 41 53 49 43 20 31 2e 30 d c 20 62 79 74 65 73 20 66 72 65 65 d 5 52 45 41 44 59 9 53 65 61 72 63
  //   68 69 6e 67 7 4c 6f 61 64 69 6e 67 3b 50 69 78 69 65 20 41 52 54 20 1c 1d 1e 1f 20 74 6f 20 6d 6f 76
  //   65 2c 20 47 52 41 2b 6b 65 79 20 74 6f 20 64 72 61 77 2c 20 43 4f 4c 2b 6b 65 79 20 66 6f 72 20 63
  //   6f 6c 6f 72 12 50 72 65 73 73 20 50 4c 41 59 20 6f 6e 20 54 41 50 45 12 50 72 65 73 73 20 53 54 4f
  //   50 20 6f 6e 20 54 41 50 45 7 45 78 70 65 63 74 20 6 53 79 6e 74 61 78 3 44 49 56 3 4f 56 46 3 50 52
  //   47 3 56 41 52 3 54 59 50 3 52 4e 47 7 20 45 72 72 6f 72 d 5 42 6c 6f 63 6b 6 45 73 63 61 70 65 0 0
  //   1a 1a 1a 24 31 3a 3e 49 49 52 52 52 60 65 6a 73 87 87 a6 ac ac b2 b2 b7 b7 b7 43 4c 53 81 43 4c 4f
  //   53 45 c2 44 41 54 41 83 44 49 4d 84 44 45 46 c5 45 4c 53 45 86 45 4e 44 c7 46 4f 52 c8 47 4f 54 4f
  //   89 47 4f 53 55 42 ca 49 46 8b 49 4e 50 55 54 cc 4c 45 54 8d 4c 49 4e 45 8e 4c 4f 41 44 cf 4d 4f 44
  //   45 d0 4e 45 58 54 d1 4f 50 54 92 4f 50 45 4e d3 50 55 54 94 50 52 49 4e 54 95 50 4c 4f 54 96 50 4f
  //   4b 45 d7 52 45 41 44 98 52 45 50 45 41 54 99 52 45 53 54 4f 52 45 9a 52 45 54 55 52 4e 9b 52 45 4d
  //   dc 53 4f 55 4e 44 dd 55 4e 54 49 4c de 57 41 49 54 df 0 1a 1e 24 29 2d 31 36 3a 3e 43 49 4c 52 56 5b
  //   60 65 6a 6e 73 77 7d 82 87 8c 93 9b a2 a6 ac b2 84 c6 85 c0 86 c1 a2 0 88 c8 e6 c0 a1 c0 d9 0 1 f0
  //   f6 10 2 38 60 e6 c0 a1 c0 10 fa e6 c0 a4 c6 a 10 e4 18 60 0 0 0 1a 22 26 2b 2b 2f 32 36 36 41 45 49
  //   53 58 58 58 5f 5f 6a 83 8c 90 4*99 41 42 53 c0 41 53 43 81 42 54 4e 82 43 48 52 24 83 45 4f 46 84 46
  //   4e 85 47 45 54 86 49 4e 53 54 52 24 c7 49 4e 54 88 4a 4f 59 89 4b 45 59 8a 4c 45 4e cb 4c 45 46 54
  //   24 8c 4d 49 44 24 8d 50 4f 53 ce 50 49 8f 52 49 47 48 54 24 d0 52 4e 44 91 53 43 4e d2 53 54 52 49
  //   4e 47 24 d3 53 54 52 24 d4 53 51 52 d5 53 47 4e 96 54 49 4d 45 d7 54 4f 50 98 55 53 52 99 56 41 4c
  //   da 56 50 4f 53 9b 0 4e 4f 54 ad 41 4e 44 bd 44 49 56 b3 45 4f 52 bf 4d 4f 44 b4 4f 52 be 41 54 ff 54
  //   4f ff 53 54 45 50 ff 54 48 45 4e ff 53 50 43 83 54 41 42 84 46 4e 0 1a 1e 22 26 2b 2f 32 36 3d 41 45
  //   49 4d 53 58 5c 5f 66 6a 6e 76 7b 7f 83 88 8c 90 94 9a 9e a2 a6 aa ae a5 7e 85 c2 a6 7e 9d 0 1 e6 7e
  //   30 1 60 a0 d5 4c 93 f0 0 0 3 2 5 d 9 0 6 11 11 8 b 4 41 e 11 7 21 83 31 c 21 21 a 0 11 0 2 c1 11 11
  //   4 5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
  //   Row of 32
  //   Data from memory latched at \CLK
  //   U45-U57 (+U39)
  //   U39 8-bit Shift Register
  //   U53
  //   VDP Latch
  //   5 Pixel Pipe + 7 Color/2bpp
  //   U45 Dual D-FF 74LS74 (Delay/Clocking)
  //   U53 8-bit Register 74LS273 (VDP Latch)
  //   U54 Quad 1-of-2 MUX 74LS157 (Char Bypass MUX)
  //   U55 Quad 1-of-2 MUX 74LS157 (Char Bypass MUX)
  //   U46 Dual 1-of-4 74LS153 (Palette MUX)
  //   U47 Dual 1-of-4 74LS153 (Palette MUX)
  //   U48 4-bit DFF with Clear 74LS175 (FG)
  //   U49 4-bit DFF with Clear 74LS175 (BG)
  //   U50 Quad 1-of-2 MUX 74LS157 (FG)
  //   U51 Quad 1-of-2 MUX 74LS157 (BG)
  //   U52 8-bit Register 74LS273 (Color 2/3)
  //   U56 Triple 3-AND 74LS11 (Color Decode)
  //   U57 Quad 2-AND 74LS08 (Color Decode)
  //   U58 Quad 2-OR 74LS32 (Color Decode)
  //   U59 Hex NOT 74LS04 (Color Decode)
endmodule

// DBUS
module PSG (
  input  HSync,
  input  nPHI2,
  input  nWR,
  input  [7:0] DBUS,
  output SND
);

  wire CounterHi_pin1, CounterHi_pin7, CounterHi_pin9, CounterHi_pin15, CounterLo_pin1, CounterLo_pin7,
       FreqLatch_pin2, FreqLatch_pin5, FreqLatch_pin6, FreqLatch_pin9, FreqLatch_pin12, FreqLatch_pin15,
       FreqLatch_pin16, FreqLatch_pin19;

  _74377 #(.ShowInternalStructure("true")) FreqLatch (
    .pin1(nWR), .pin2(FreqLatch_pin2), .pin3(DBUS[0]), .pin4(DBUS[1]), .pin5(FreqLatch_pin5),
    .pin6(FreqLatch_pin6), .pin7(DBUS[2]), .pin8(DBUS[3]), .pin9(FreqLatch_pin9), .pin19(FreqLatch_pin19),
    .pin18(DBUS[7]), .pin17(DBUS[6]), .pin16(FreqLatch_pin16), .pin15(FreqLatch_pin15), .pin14(DBUS[5]),
    .pin13(DBUS[4]), .pin12(FreqLatch_pin12), .pin11(nPHI2));
  _74161 #(.ShowInternalStructure("true")) CounterHi (
    .pin1(CounterHi_pin1), .pin2(HSync), .pin3(FreqLatch_pin12), .pin4(FreqLatch_pin15),
    .pin5(FreqLatch_pin16), .pin6(FreqLatch_pin19), .pin7(CounterHi_pin7), .pin15(CounterHi_pin15),
    .pin10(CounterHi_pin7), .pin9(CounterHi_pin9));  // open: pin14, pin13, pin12, pin11
  _74161 #(.ShowInternalStructure("true")) CounterLo (
    .pin1(CounterLo_pin1), .pin2(HSync), .pin3(FreqLatch_pin2), .pin4(FreqLatch_pin5), .pin5(FreqLatch_pin6),
    .pin6(FreqLatch_pin9), .pin7(CounterLo_pin7), .pin15(CounterHi_pin7), .pin10(CounterLo_pin7),
    .pin9(CounterHi_pin9));  // open: pin14, pin13, pin12, pin11
  not not_1 (CounterHi_pin9, CounterHi_pin15);
  T_Flip_Flop t_ff_1 (.clk(HSync), .T(CounterHi_pin15), .Q(SND));  // open: Qn, preset, reset
  LED led_1 (.in(SND));
  // also tied to VCC on the sheet: {CounterHi_pin1, CounterLo_pin1, CounterLo_pin7}

  // Notes on the sheet:
  //   nWR: initial=0x1
  //   DBUS: initial=0x80
  //   Note: if using 374, NOR nWR with nPHI2
  //   IO address decode
  //   Rising Edge as PHI2 falls
  //   74LS374 ?
  //   15720 Hz
  //   DIV 2
endmodule

module SN74LS298 (
  input  WS,
  input  A1,
  input  B1,
  input  C1,
  input  D1,
  input  A2,
  input  B2,
  input  C2,
  input  D2,
  input  CLK,
  output QA,
  output QB,
  output QC,
  output QD
);

  wire n74157_1_pin4, n74157_1_pin7, n74157_1_pin9, n74157_1_pin12, n74157_1_pin15, n74175_1_pin1;

  _74157 #(.ShowInternalStructure("true")) u_74157_1 (
    .pin1(WS), .pin2(A1), .pin3(A2), .pin4(n74157_1_pin4), .pin5(B1), .pin6(B2), .pin7(n74157_1_pin7),
    .pin15(n74157_1_pin15), .pin14(D1), .pin13(D2), .pin12(n74157_1_pin12), .pin11(C1), .pin10(C2),
    .pin9(n74157_1_pin9));
  _74175 #(.ShowInternalStructure("true")) u_74175_1 (
    .pin1(n74175_1_pin1), .pin2(QA), .pin4(n74157_1_pin4), .pin5(n74157_1_pin7), .pin7(QB), .pin15(QD),
    .pin13(n74157_1_pin12), .pin12(n74157_1_pin9), .pin10(QC), .pin9(CLK));  // open: pin3, pin6, pin14, pin11
  // also tied to GND on the sheet: n74157_1_pin15
  // also tied to VCC on the sheet: n74175_1_pin1

  // Notes on the sheet:
  //   74LS175
endmodule
